// Logisim project main.circ as structural Verilog: 4 circuits, main circuit GPU_MEM_4B
module main (
);

  wire c, clock_1_out, clock_2_out;
  wire [7:0] counter_1_q, rom_1_data;
  wire [31:0] gpu_1_out_6, gpu_1_out_7, gpu_1_out_8, gpu_1_out_9, gpu_1_out_10, gpu_1_out_11, gpu_1_out_12,
       gpu_1_out_13, gpu_1_out_14, gpu_1_out_15, gpu_1_out_16, gpu_1_out_17, gpu_1_out_18, gpu_1_out_19,
       gpu_1_out_20, gpu_1_out_21, gpu_1_out_22, gpu_1_out_23, gpu_1_out_24, gpu_1_out_25, gpu_1_out_26,
       gpu_1_out_27, gpu_1_out_28, gpu_1_out_29, gpu_1_out_30, gpu_1_out_31, gpu_1_out_32, gpu_1_out_33,
       gpu_1_out_34, gpu_1_out_35, gpu_1_out_36, gpu_1_out_37;

  Clock clock_1 (.out(clock_1_out));
  Clock clock_2 (.out(clock_2_out));
  ROM rom_1 (.addr(counter_1_q), .data(rom_1_data));
  Counter counter_1 (.Q(counter_1_q), .clk(clock_1_out), .clr(c));  // open: load, D, count, carry, up
  Button button_1 (.out(c));
  DotMatrix #(.inputtype("row"), .matrixcols(32), .matrixrows(32)) dotmatrix_1 (
    .row0(gpu_1_out_6), .row1(gpu_1_out_7), .row2(gpu_1_out_8), .row3(gpu_1_out_9), .row4(gpu_1_out_10),
    .row5(gpu_1_out_11), .row6(gpu_1_out_12), .row7(gpu_1_out_13), .row8(gpu_1_out_14), .row9(gpu_1_out_15),
    .row10(gpu_1_out_16), .row11(gpu_1_out_17), .row12(gpu_1_out_18), .row13(gpu_1_out_19),
    .row14(gpu_1_out_20), .row15(gpu_1_out_21), .row16(gpu_1_out_22), .row17(gpu_1_out_23),
    .row18(gpu_1_out_24), .row19(gpu_1_out_25), .row20(gpu_1_out_26), .row21(gpu_1_out_27),
    .row22(gpu_1_out_28), .row23(gpu_1_out_29), .row24(gpu_1_out_30), .row25(gpu_1_out_31),
    .row26(gpu_1_out_32), .row27(gpu_1_out_33), .row28(gpu_1_out_34), .row29(gpu_1_out_35),
    .row30(gpu_1_out_36), .row31(gpu_1_out_37));
  GPU gpu_1 (
    .out_6(gpu_1_out_6), .out_7(gpu_1_out_7), .out_8(gpu_1_out_8), .out_9(gpu_1_out_9),
    .out_10(gpu_1_out_10), .out_11(gpu_1_out_11), .out_12(gpu_1_out_12), .out_13(gpu_1_out_13),
    .out_14(gpu_1_out_14), .out_15(gpu_1_out_15), .out_16(gpu_1_out_16), .out_17(gpu_1_out_17),
    .out_18(gpu_1_out_18), .out_19(gpu_1_out_19), .out_20(gpu_1_out_20), .out_21(gpu_1_out_21),
    .out_22(gpu_1_out_22), .out_23(gpu_1_out_23), .out_24(gpu_1_out_24), .out_25(gpu_1_out_25),
    .out_26(gpu_1_out_26), .out_27(gpu_1_out_27), .out_28(gpu_1_out_28), .out_29(gpu_1_out_29),
    .out_30(gpu_1_out_30), .out_31(gpu_1_out_31), .out_32(gpu_1_out_32), .out_33(gpu_1_out_33),
    .out_34(gpu_1_out_34), .out_35(gpu_1_out_35), .out_36(gpu_1_out_36), .out_37(gpu_1_out_37),
    .Data(rom_1_data), .Clock(clock_2_out), .Clear(c), .Address(counter_1_q), .Enable(1'b1));

  // Notes on the sheet:
  //   contents of rom_1 (hex, n*v repeats v):
  //   4*ff 80 0 0 1 80 0 0 1 80 3 e0 1 80 c 10 1 80 10 10 1 80 20 fc 1 80 43 fe 1 80 4c c 1 80 fc 58 1 80
  //   8c 5c 1 80 8e 2 1 80 84 82 1 80 41 e7 1 80 30 7c 1 80 78 10 1 80 8f e0 1 80 8f 34 1 81 10 9a 1 81 20
  //   4a 1 81 20 4c 1 81 90 b4 1 80 ff 34 1 80 ff fc 1 80 7f fe 1 80 bf f9 1 80 bf 71 1 80 9e 62 1 80 41
  //   24 1 80 3f 18 1 80 0 0 1 8*ff 80 0 0 1 80 0 0 1 80 3 e0 1 80 c 10 1 80 10 10 1 80 20 fc 1 80 43 fe 1
  //   80 4c c 1 80 fc 58 1 80 8c 5c 1 80 8e 2 1 80 84 82 1 80 41 e7 1 80 30 7c 1 80 78 10 1 80 8f e0 1 80
  //   8f 34 1 81 10 9a 1 81 20 4a 1 81 20 4c 1 81 90 b4 1 80 ff 34 1 80 ff fc 1 80 7f fe 1 80 bf f9 1 80
  //   bf 71 1 80 9e 62 1 80 41 24 1 80 3f 18 1 80 0 0 1 4*ff
endmodule

module GPU (
  input  [7:0] Data,
  input  Clock,
  input  Clear,
  input  [7:0] Address,
  input  Enable,
  output [31:0] out_6,
  output [31:0] out_7,
  output [31:0] out_8,
  output [31:0] out_9,
  output [31:0] out_10,
  output [31:0] out_11,
  output [31:0] out_12,
  output [31:0] out_13,
  output [31:0] out_14,
  output [31:0] out_15,
  output [31:0] out_16,
  output [31:0] out_17,
  output [31:0] out_18,
  output [31:0] out_19,
  output [31:0] out_20,
  output [31:0] out_21,
  output [31:0] out_22,
  output [31:0] out_23,
  output [31:0] out_24,
  output [31:0] out_25,
  output [31:0] out_26,
  output [31:0] out_27,
  output [31:0] out_28,
  output [31:0] out_29,
  output [31:0] out_30,
  output [31:0] out_31,
  output [31:0] out_32,
  output [31:0] out_33,
  output [31:0] out_34,
  output [31:0] out_35,
  output [31:0] out_36,
  output [31:0] out_37
);

  wire demultiplexer_1_out0, demultiplexer_1_out1, demultiplexer_1_out2, demultiplexer_1_out3,
       gpu_mem_32b_1_clear_out, gpu_mem_32b_1_clock_out, gpu_mem_32b_2_clear_out, gpu_mem_32b_2_clock_out,
       gpu_mem_32b_3_clear_out, gpu_mem_32b_3_clock_out;
  wire [4:0] undriven, undriven_2, undriven_3;
  wire [7:0] gpu_mem_32b_1_data_out, gpu_mem_32b_2_data_out, gpu_mem_32b_3_data_out;

  Demultiplexer #(.enable("false"), .select(2)) demultiplexer_1 (
    .out0(demultiplexer_1_out0), .out1(demultiplexer_1_out1), .out2(demultiplexer_1_out2),
    .out3(demultiplexer_1_out3), .in(Enable), .sel(Address[6:5]));
  GPU_MEM_32B gpu_mem_32b_1 (
    .Address({undriven[4], Address[4], undriven[3], Address[3], undriven[2], Address[2], undriven[1], Address[1], undriven[0], Address[0]}),
    .Clock_out(gpu_mem_32b_1_clock_out), .Clear_out(gpu_mem_32b_1_clear_out),
    .Data_out(gpu_mem_32b_1_data_out), .out_14(out_10), .out_15(out_11), .out_16(out_12), .out_17(out_13),
    .out_10(out_6), .out_11(out_7), .out_12(out_8), .out_13(out_9), .Clock(Clock), .Clear(Clear),
    .Data(Data), .Enable(demultiplexer_1_out0));
  GPU_MEM_32B gpu_mem_32b_2 (
    .Address({undriven_2[4], undriven[4], undriven_2[3], undriven[3], undriven_2[2], undriven[2], undriven_2[1], undriven[1], undriven_2[0], undriven[0]}),
    .Clock_out(gpu_mem_32b_2_clock_out), .Clear_out(gpu_mem_32b_2_clear_out),
    .Data_out(gpu_mem_32b_2_data_out), .out_14(out_18), .out_15(out_19), .out_16(out_20), .out_17(out_21),
    .out_10(out_14), .out_11(out_15), .out_12(out_16), .out_13(out_17), .Clock(gpu_mem_32b_1_clock_out),
    .Clear(gpu_mem_32b_1_clear_out), .Data(gpu_mem_32b_1_data_out), .Enable(demultiplexer_1_out1));
  GPU_MEM_32B gpu_mem_32b_3 (
    .Address({undriven_3[4], undriven_2[4], undriven_3[3], undriven_2[3], undriven_3[2], undriven_2[2], undriven_3[1], undriven_2[1], undriven_3[0], undriven_2[0]}),
    .Clock_out(gpu_mem_32b_3_clock_out), .Clear_out(gpu_mem_32b_3_clear_out),
    .Data_out(gpu_mem_32b_3_data_out), .out_14(out_26), .out_15(out_27), .out_16(out_28), .out_17(out_29),
    .out_10(out_22), .out_11(out_23), .out_12(out_24), .out_13(out_25), .Clock(gpu_mem_32b_2_clock_out),
    .Clear(gpu_mem_32b_2_clear_out), .Data(gpu_mem_32b_2_data_out), .Enable(demultiplexer_1_out2));
  GPU_MEM_32B gpu_mem_32b_4 (
    .Address({1'bz, undriven_3[4], 1'bz, undriven_3[3], 1'bz, undriven_3[2], 1'bz, undriven_3[1], 1'bz, undriven_3[0]}),
    .out_14(out_34), .out_15(out_35), .out_16(out_36), .out_17(out_37), .out_10(out_30), .out_11(out_31),
    .out_12(out_32), .out_13(out_33), .Clock(gpu_mem_32b_3_clock_out), .Clear(gpu_mem_32b_3_clear_out),
    .Data(gpu_mem_32b_3_data_out), .Enable(demultiplexer_1_out3));  // open: Clock_out, Clear_out, Data_out

  // Other names for the same wires on the sheet: a2[4:0] = Address[4:0]; a1[1:0] = Address[6:5]; c = Clear;
  //   clk = Clock; d[7:0] = Data
endmodule

module GPU_MEM_32B (
  input  [7:0] Data,
  input  Clock,
  input  Clear,
  input  [4:0] Address,
  input  Enable,
  output [7:0] Data_out,
  output Clock_out,
  output Clear_out,
  output [4:0] Address_out,
  output [31:0] out_10,
  output [31:0] out_11,
  output [31:0] out_12,
  output [31:0] out_13,
  output [31:0] out_14,
  output [31:0] out_15,
  output [31:0] out_16,
  output [31:0] out_17
);

  wire demultiplexer_1_out0, demultiplexer_1_out1, demultiplexer_1_out2, demultiplexer_1_out3,
       demultiplexer_1_out4, demultiplexer_1_out5, demultiplexer_1_out6, demultiplexer_1_out7;

  Demultiplexer #(.enable("false"), .select(3)) demultiplexer_1 (
    .out0(demultiplexer_1_out0), .out1(demultiplexer_1_out1), .out2(demultiplexer_1_out2),
    .out3(demultiplexer_1_out3), .out4(demultiplexer_1_out4), .out5(demultiplexer_1_out5),
    .out6(demultiplexer_1_out6), .out7(demultiplexer_1_out7), .in(Enable), .sel(Address[4:2]));
  GPU_MEM_4B gpu_mem_4b_1 (
    .Value(out_10), .Data(Data), .Clock(Clock), .Clear(Clear), .Address(Address[1:0]),
    .Enable(demultiplexer_1_out0));
  GPU_MEM_4B gpu_mem_4b_2 (
    .Value(out_11), .Data(Data), .Clock(Clock), .Clear(Clear), .Address(Address[1:0]),
    .Enable(demultiplexer_1_out1));
  GPU_MEM_4B gpu_mem_4b_3 (
    .Value(out_12), .Data(Data), .Clock(Clock), .Clear(Clear), .Address(Address[1:0]),
    .Enable(demultiplexer_1_out2));
  GPU_MEM_4B gpu_mem_4b_4 (
    .Value(out_13), .Data(Data), .Clock(Clock), .Clear(Clear), .Address(Address[1:0]),
    .Enable(demultiplexer_1_out3));
  GPU_MEM_4B gpu_mem_4b_5 (
    .Value(out_14), .Data(Data), .Clock(Clock), .Clear(Clear), .Address(Address[1:0]),
    .Enable(demultiplexer_1_out4));
  GPU_MEM_4B gpu_mem_4b_6 (
    .Value(out_15), .Data(Data), .Clock(Clock), .Clear(Clear), .Address(Address[1:0]),
    .Enable(demultiplexer_1_out5));
  GPU_MEM_4B gpu_mem_4b_7 (
    .Value(out_16), .Data(Data), .Clock(Clock), .Clear(Clear), .Address(Address[1:0]),
    .Enable(demultiplexer_1_out6));
  GPU_MEM_4B gpu_mem_4b_8 (
    .Value(out_17), .Data(Data), .Clock(Clock), .Clear(Clear), .Address(Address[1:0]),
    .Enable(demultiplexer_1_out7));

  assign Address_out = Address;
  assign Clear_out = Clear;
  assign Clock_out = Clock;
  assign Data_out = Data;

  // Other names for the same wires on the sheet: a2[1:0] = Address[1:0]; a1[2:0] = Address[4:2]; c = Clear;
  //   clk = Clock; d[7:0] = Data
endmodule

module GPU_MEM_4B (
  input  [7:0] Data,
  input  Clock,
  input  Clear,
  input  [1:0] Address,
  input  Enable,
  output [31:0] Value
);

  wire demultiplexer_1_out0, demultiplexer_1_out1, demultiplexer_1_out2, demultiplexer_1_out3;

  Demultiplexer #(.enable("false"), .select(2)) demultiplexer_1 (
    .out0(demultiplexer_1_out0), .out1(demultiplexer_1_out1), .out2(demultiplexer_1_out2),
    .out3(demultiplexer_1_out3), .in(Enable), .sel(Address));
  Register register_1 (.D(Data), .en(demultiplexer_1_out0), .clk(Clock), .Q(Value[31:24]), .clr(Clear));
  Register register_2 (.D(Data), .en(demultiplexer_1_out1), .clk(Clock), .Q(Value[23:16]), .clr(Clear));
  Register register_3 (.D(Data), .en(demultiplexer_1_out2), .clk(Clock), .Q(Value[15:8]), .clr(Clear));
  Register register_4 (.D(Data), .en(demultiplexer_1_out3), .clk(Clock), .Q(Value[7:0]), .clr(Clear));

  // Other names for the same wires on the sheet: a[1:0] = Address; c = Clear; clk = Clock; d[7:0] = Data
endmodule
